# Fritzing sketch joy-stick.fritzing (saved by Fritzing 0.9.3b)

parts:
  Part1 = Arduino Mega 2560 (Rev3)
  U1 = JOYSTICK-PSP1000 [package=joystick-psp1000]

nets:
  N1: Part1.A1, U1.Y
  N2: Part1.A2, U1.X
  5V: Part1.5V, U1.VCC
  GND: Part1.GND, U1.GND
