# Fritzing sketch Motion_sensor_ultrasonic-sensor+LED+Buzzer (saved by Fritzing 0.9.3b)
circuit board: 8.46667cm x 5.64444cm
breadboards: 1

parts:
  R1 = Resistor [tolerance=±5% resistance=220 package=THT]
  R2 = Resistor [tolerance=±5% resistance=220 package=THT]
  R3 = Resistor [tolerance=±5% resistance=220 package=THT]
  LED1 = LED - 5mm [color="Red (633nm)" package="5 mm [THT]"]
  HC-SR04_Sensor_1 = HC-SR04 Ultrasonic Distance Sensor
  Part1 = Arduino Mega 2560 (Rev3)
  LED2 = RGB LED (com. cathode, rgb) [package="5 mm [THT]"]
  J1 = Piezo Speaker

nets:
  N1: R1.Pin_0, Part1.D9_PWM
  N2: R1.Pin_1, LED2.green_anode
  N3: R2.Pin_0, LED1.anode
  N4: R2.Pin_1, Part1.D8_PWM
  N5: R3.Pin_0, Part1.D7_PWM
  N6: R3.Pin_1, J1.pin2
  N7: LED1.cathode, HC-SR04_Sensor_1.GND, LED2.common_cathode, J1.pin1
  VCC: HC-SR04_Sensor_1.VCC, Part1.5V
  N8: HC-SR04_Sensor_1.TRIG, Part1.D12_PWM
  N9: HC-SR04_Sensor_1.ECHO, Part1.D10_PWM

// code stored in the sketch: ultrasonic-fritzing.ino
/*
* Ultrasonic Sensor HC-SR04 and Arduino Tutorial
*
* by Eng_Mark..
*
*/
//defines pins numbers

const int trigPin = 12;
const int echoPin = 10;
const int led=9;
const int BUZZER=8;
const int ledR=7;

// defines variables

long duration;
int distance;

void setup() 
{
pinMode(trigPin, OUTPUT); // Sets the trigPin as an Output
pinMode(echoPin, INPUT); // Sets the echoPin as an Input
Serial.begin(9600); // Starts the serial communication
pinMode(led, OUTPUT);
pinMode(BUZZER, OUTPUT);
pinMode(ledR, OUTPUT);

}
void loop() 
{
// Clears the trigPin
digitalWrite(trigPin, LOW);
delayMicroseconds(2);

// Sets the trigPin on HIGH state for 10 micro seconds
digitalWrite(trigPin, HIGH);
delayMicroseconds(100);
digitalWrite(trigPin, LOW);

// Reads the echoPin, returns the sound wave travel time in microseconds
duration = pulseIn(echoPin, HIGH);

// Calculating the distance
distance= duration*0.034/2;

//conditions for led
if(distance>100)
{
  digitalWrite(led, LOW);
} 
else{
 digitalWrite(led, HIGH);
}
//conditions for ledR
if(distance>75)
{
  digitalWrite(ledR, LOW);
} 
else{
 digitalWrite(ledR, HIGH);
}

//conditions for BUZZER
if(distance>45)
{
  digitalWrite(BUZZER, LOW);
} 
else{
 digitalWrite(BUZZER, HIGH);
}

// Prints the distance on the Serial Monitor
Serial.print("Distance: ");
Serial.println(distance);
Serial.print("cm");
}
